// Digital circuit mainBus.dig as structural Verilog
module mainBus (
  input  clk,
  input  [7:0] in_2
);

  wire dipswitch_1_out, dipswitch_2_out, dipswitch_3_out, dipswitch_4_out;
  wire [7:0] undriven;

  DipSwitch dipswitch_1 (.out(dipswitch_1_out));
  DipSwitch dipswitch_2 (.out(dipswitch_2_out));
  DipSwitch dipswitch_3 (.out(dipswitch_3_out));
  DipSwitch dipswitch_4 (.out(dipswitch_4_out));
  _5bitPC2 _5bitpc2_1 (
    .PC_in(in_2), .Le_a(dipswitch_1_out), .CNTe_a(dipswitch_2_out), .CLK(clk), .CLR(dipswitch_3_out),
    .Re_a(dipswitch_4_out));  // open: PC_out
  Seven_Seg_Hex seven_seg_hex_1 (.d(undriven[7:4]), .dp(1'b0));
  Seven_Seg_Hex seven_seg_hex_2 (.d(undriven[3:0]), .dp(1'b0));

  // Notes on the sheet:
  //   in_2: default 5
endmodule
